// Digital circuit alu.dig as structural Verilog
module alu (
  input  [7:0] A,
  input  [7:0] B,
  input  [4:0] Opcode,
  output [7:0] O
);

  wire [7:0] add_1_s, add_2_s, and_1_out, barrelshifter_1_out, barrelshifter_2_out, div_1_q, mul_1_mul,
       not_1_out, or_1_out, sub_1_s, sub_2_s, xor_1_out;
  wire [7:3] comparator_3_eq, sub_2_c_o;
  wire [15:8] mul_1_mul_2;

  BarrelShifter #(.Bits(8)) barrelshifter_1 (.in(A), .shift(B[3:0]), .out(barrelshifter_1_out));
  BarrelShifter #(.Bits(8), .direction("right")) barrelshifter_2 (.in(A), .shift(B[3:0]), .out(barrelshifter_2_out));
  Add #(.Bits(8)) add_1 (.a(A), .b(8'h1), .c_i(1'b0), .s(add_1_s));  // open: c_o
  Sub #(.Bits(8)) sub_1 (.a(A), .b(8'h1), .c_i(1'b0), .s(sub_1_s));  // open: c_o
  Add #(.Bits(8)) add_2 (.a(A), .b(B), .c_i(1'b0), .s(add_2_s));  // open: c_o
  Sub #(.Bits(8)) sub_2 (.a(A), .b(B), .c_i(1'b0), .s(sub_2_s), .c_o(sub_2_c_o[5]));
  Mul #(.Bits(8)) mul_1 (.a(A), .b(B), .mul({mul_1_mul_2, mul_1_mul}));
  Div #(.Bits(8)) div_1 (.a(A), .b(B), .q(div_1_q));  // open: r
  assign not_1_out = ~A;  // Not not_1, 8 bits wide
  assign and_1_out = A & B;  // And and_1, 8 bits wide
  assign or_1_out = A | B;  // Or or_1, 8 bits wide
  assign xor_1_out = A ^ B;  // XOr xor_1, 8 bits wide
  Comparator #(.Bits(8)) comparator_1 (.a(A), .b(B), .lt(sub_2_c_o[6]));  // open: gt, eq
  Multiplexer #(.Selector_Bits(4), .Bits(8)) multiplexer_1 (
    .sel(Opcode[3:0]), .in_0(add_2_s), .in_1(sub_2_s), .in_2(mul_1_mul), .in_3(div_1_q), .in_4(not_1_out),
    .in_5(and_1_out), .in_6(or_1_out), .in_7(xor_1_out), .in_8(barrelshifter_1_out),
    .in_9(barrelshifter_2_out), .in_10(add_1_s), .in_11(sub_1_s),
    .in_12({comparator_3_eq[7], 2'b00, and_1_out[7], comparator_3_eq[3], 3'b000}),
    .in_13({sub_2_c_o[7:5], sub_2_s[7], sub_2_c_o[3], 3'b000}), .in_14({8{1'b0}}), .in_15({8{1'b0}}), .out(O));
  Comparator #(.Bits(8)) comparator_2 (.a(sub_2_s), .b({8{1'b0}}), .eq(sub_2_c_o[7]));  // open: gt, lt
  Comparator #(.Bits(8)) comparator_3 (.a(and_1_out), .b({8{1'b0}}), .eq(comparator_3_eq[7]));  // open: gt, lt
  not not_2 (sub_2_c_o[3], sub_2_s[0]);
  not not_3 (comparator_3_eq[3], and_1_out[0]);
endmodule
