// Digital circuit decoder.dig as structural Verilog
module decoder (
  input  [19:0] Inst,
  output [4:0] Opcode,
  output [2:0] Reg_1,
  output [2:0] Reg_2,
  output [7:0] Val_IMMPTR,
  output Mode
);


  assign Mode = Inst[0];
  assign Opcode = Inst[19:15];
  assign Reg_1 = Inst[14:12];
  assign Reg_2 = Inst[11:9];
  assign Val_IMMPTR = Inst[8:1];

  // Notes on the sheet:
  //   Inst: Raw Instruction Bytes
endmodule
