// Digital circuit exec.dig as structural Verilog
module exec (
  input  [4:0] Opcode,
  input  [7:0] Da_RF,
  input  [7:0] Db_RF,
  input  [2:0] Reg_1,
  input  [2:0] Reg_2,
  input  [7:0] Val_IMMPTR,
  input  [7:0] Q_RAM,
  input  [7:0] O_ALU,
  input  Mode,
  input  [7:0] Read_Peripherals,
  output [7:0] A_ALU,
  output [7:0] Din_RF,
  output [2:0] RW_RF,
  output WE_RF,
  output [7:0] A_RAM,
  output [7:0] D_RAM,
  output WE_RAM,
  output PC_Override,
  output [7:0] PC_OverrideVal,
  output HLT_Flag,
  output [2:0] Ra_RF,
  output [2:0] Rb_RF,
  output [7:0] B_ALU,
  output [7:0] PortN_Peripherals,
  output [7:0] Data_Peripherals,
  output Write_Peripherals,
  output ReadSig_Peripherals
);

  Comparator #(.Bits(5)) comparator_1 (.a(Opcode), .b({5{1'b1}}), .eq(HLT_Flag));  // open: gt, lt
  Multiplexer #(.Bits(8)) multiplexer_1 (.sel(Mode), .in_0(Val_IMMPTR), .in_1(Db_RF), .out(B_ALU));
  Multiplexer #(.Selector_Bits(5)) multiplexer_2 (
    .sel(Opcode), .in_0(1'b0), .in_1(1'b0), .in_2(1'b0), .in_3(1'b0), .in_4(1'b0), .in_5(1'b0), .in_6(1'b1),
    .in_7(Db_RF[7]), .in_8(Db_RF[6]), .in_9(Db_RF[5]), .in_10(Db_RF[4]), .in_11(Db_RF[3]), .in_12(1'b0),
    .in_13(1'b0), .in_14(1'b0), .in_15(1'b0), .in_16(1'b0), .in_17(1'b0), .in_18(1'b0), .in_19(1'b0),
    .in_20(1'b0), .in_21(1'b0), .in_22(1'b0), .in_23(1'b0), .in_24(1'b0), .in_25(1'b0), .in_26(1'b0),
    .in_27(1'b0), .in_28(1'b0), .in_29(1'b0), .in_30(1'b0), .in_31(1'b0), .out(PC_Override));
  Multiplexer #(.Selector_Bits(5), .Bits(8)) multiplexer_3 (
    .sel(Opcode), .in_0({8{1'b0}}), .in_1(Val_IMMPTR), .in_2(Q_RAM), .in_3(Db_RF), .in_4({8{1'b0}}),
    .in_5({8{1'b0}}), .in_6({8{1'b0}}), .in_7({8{1'b0}}), .in_8({8{1'b0}}), .in_9({8{1'b0}}),
    .in_10({8{1'b0}}), .in_11({8{1'b0}}), .in_12(Read_Peripherals), .in_13({8{1'b0}}), .in_14({8{1'b0}}),
    .in_15({8{1'b0}}), .in_16(O_ALU), .in_17(O_ALU), .in_18(O_ALU), .in_19(O_ALU), .in_20(O_ALU),
    .in_21(O_ALU), .in_22(O_ALU), .in_23(O_ALU), .in_24(O_ALU), .in_25(O_ALU), .in_26(O_ALU), .in_27(O_ALU),
    .in_28(O_ALU), .in_29(O_ALU), .in_30(O_ALU), .in_31({8{1'b0}}), .out(Din_RF));
  Multiplexer #(.Bits(8)) multiplexer_4 (.sel(Mode), .in_0(Val_IMMPTR), .in_1(Db_RF), .out(PortN_Peripherals));
  Multiplexer #(.Selector_Bits(5), .Bits(3)) multiplexer_5 (
    .sel(Opcode), .in_0(Reg_2), .in_1(Reg_2), .in_2(Reg_2), .in_3(Reg_2), .in_4(Reg_2), .in_5(Reg_2),
    .in_6(3'b111), .in_7(3'b111), .in_8(3'b111), .in_9(3'b111), .in_10(3'b111), .in_11(3'b111),
    .in_12(Reg_2), .in_13(Reg_2), .in_14(Reg_2), .in_15(Reg_2), .in_16(Reg_2), .in_17(Reg_2), .in_18(Reg_2),
    .in_19(Reg_2), .in_20(Reg_2), .in_21(Reg_2), .in_22(Reg_2), .in_23(Reg_2), .in_24(Reg_2), .in_25(Reg_2),
    .in_26(Reg_2), .in_27(Reg_2), .in_28(Reg_2), .in_29(Reg_2), .in_30(Reg_2), .in_31(3'b000), .out(Rb_RF));
  Multiplexer #(.Selector_Bits(5), .Bits(8)) multiplexer_6 (
    .sel(Opcode), .in_0({8{1'b0}}), .in_1({8{1'b0}}), .in_2(PortN_Peripherals), .in_3({8{1'b0}}),
    .in_4(Da_RF), .in_5(Da_RF), .in_6({8{1'b0}}), .in_7({8{1'b0}}), .in_8({8{1'b0}}), .in_9({8{1'b0}}),
    .in_10({8{1'b0}}), .in_11({8{1'b0}}), .in_12({8{1'b0}}), .in_13({8{1'b0}}), .in_14({8{1'b0}}),
    .in_15({8{1'b0}}), .in_16({8{1'b0}}), .in_17({8{1'b0}}), .in_18({8{1'b0}}), .in_19({8{1'b0}}),
    .in_20({8{1'b0}}), .in_21({8{1'b0}}), .in_22({8{1'b0}}), .in_23({8{1'b0}}), .in_24({8{1'b0}}),
    .in_25({8{1'b0}}), .in_26({8{1'b0}}), .in_27({8{1'b0}}), .in_28({8{1'b0}}), .in_29({8{1'b0}}),
    .in_30({8{1'b0}}), .in_31({8{1'b0}}), .out(A_RAM));
  Multiplexer #(.Selector_Bits(5)) multiplexer_7 (
    .sel(Opcode), .in_0(1'b0), .in_1(1'b1), .in_2(1'b1), .in_3(1'b1), .in_4(1'b0), .in_5(1'b0), .in_6(1'b0),
    .in_7(1'b0), .in_8(1'b0), .in_9(1'b0), .in_10(1'b0), .in_11(1'b0), .in_12(1'b1), .in_13(1'b0),
    .in_14(1'b0), .in_15(1'b0), .in_16(1'b1), .in_17(1'b1), .in_18(1'b1), .in_19(1'b1), .in_20(1'b1),
    .in_21(1'b1), .in_22(1'b1), .in_23(1'b1), .in_24(1'b1), .in_25(1'b1), .in_26(1'b1), .in_27(1'b1),
    .in_28(1'b1), .in_29(1'b1), .in_30(1'b0), .in_31(1'b0), .out(WE_RF));
  Multiplexer #(.Selector_Bits(5), .Bits(3)) multiplexer_8 (
    .sel(Opcode), .in_0(3'b000), .in_1(Reg_1), .in_2(Reg_1), .in_3(Reg_1), .in_4(3'b000), .in_5(3'b000),
    .in_6(3'b000), .in_7(3'b000), .in_8(3'b000), .in_9(3'b000), .in_10(3'b000), .in_11(3'b000),
    .in_12(Reg_1), .in_13(Reg_1), .in_14(3'b000), .in_15(3'b000), .in_16(Reg_1), .in_17(Reg_1),
    .in_18(Reg_1), .in_19(Reg_1), .in_20(Reg_1), .in_21(Reg_1), .in_22(Reg_1), .in_23(Reg_1), .in_24(Reg_1),
    .in_25(Reg_1), .in_26(Reg_1), .in_27(Reg_1), .in_28(3'b111), .in_29(3'b111), .in_30(3'b000),
    .in_31(3'b000), .out(RW_RF));
  Multiplexer #(.Selector_Bits(5)) multiplexer_9 (
    .sel(Opcode), .in_0(1'b0), .in_1(1'b0), .in_2(1'b0), .in_3(1'b0), .in_4(1'b1), .in_5(1'b1), .in_6(1'b0),
    .in_7(1'b0), .in_8(1'b0), .in_9(1'b0), .in_10(1'b0), .in_11(1'b0), .in_12(1'b0), .in_13(1'b0),
    .in_14(1'b0), .in_15(1'b0), .in_16(1'b0), .in_17(1'b0), .in_18(1'b0), .in_19(1'b0), .in_20(1'b0),
    .in_21(1'b0), .in_22(1'b0), .in_23(1'b0), .in_24(1'b0), .in_25(1'b0), .in_26(1'b0), .in_27(1'b0),
    .in_28(1'b0), .in_29(1'b0), .in_30(1'b0), .in_31(1'b0), .out(WE_RAM));
  Multiplexer #(.Selector_Bits(5), .Bits(8)) multiplexer_10 (
    .sel(Opcode), .in_0({8{1'b0}}), .in_1({8{1'b0}}), .in_2({8{1'b0}}), .in_3({8{1'b0}}), .in_4(Val_IMMPTR),
    .in_5(Db_RF), .in_6({8{1'b0}}), .in_7({8{1'b0}}), .in_8({8{1'b0}}), .in_9({8{1'b0}}), .in_10({8{1'b0}}),
    .in_11({8{1'b0}}), .in_12({8{1'b0}}), .in_13({8{1'b0}}), .in_14({8{1'b0}}), .in_15({8{1'b0}}),
    .in_16({8{1'b0}}), .in_17({8{1'b0}}), .in_18({8{1'b0}}), .in_19({8{1'b0}}), .in_20({8{1'b0}}),
    .in_21({8{1'b0}}), .in_22({8{1'b0}}), .in_23({8{1'b0}}), .in_24({8{1'b0}}), .in_25({8{1'b0}}),
    .in_26({8{1'b0}}), .in_27({8{1'b0}}), .in_28({8{1'b0}}), .in_29({8{1'b0}}), .in_30({8{1'b0}}),
    .in_31({8{1'b0}}), .out(D_RAM));
  Comparator #(.Bits(5)) comparator_2 (.a(Opcode), .b(5'b01101), .eq(Write_Peripherals));  // open: gt, lt
  Comparator #(.Bits(5)) comparator_3 (.a(Opcode), .b(5'b01100), .eq(ReadSig_Peripherals));  // open: gt, lt

  assign A_ALU = Da_RF;
  assign Data_Peripherals = Da_RF;
  assign PC_OverrideVal = Val_IMMPTR;
  assign Ra_RF = Reg_1;

  // Notes on the sheet:
  //   Din_RF: Data
  //   RW_RF: Register Write Dest
endmodule
