// Digital circuit p8.dig as structural Verilog
module p8 (
  input  clk,
  output Overflow,
  output [7:0] out_2,
  output [7:0] out_3,
  output [7:0] out_4
);

  wire and_1_out, and_3_out, Clk_2, Clk_t, d_ff_1_q, decoder_1_mode, exec_1_pc_override,
       exec_1_readsig_peripherals, exec_1_we_ram, exec_1_we_rf, exec_1_write_peripherals, HLT_Flag,
       not_1_out, not_2_out, peripherals_1_interrupt;
  wire [2:0] exec_1_ra_rf, exec_1_rb_rf, exec_1_rw_rf, Reg_1, Reg_2;
  wire [4:0] decoder_1_opcode;
  wire [7:0] exec_1_a_alu, exec_1_a_ram, exec_1_b_alu, exec_1_d_ram, exec_1_data_peripherals, exec_1_din_rf,
       exec_1_pc_overrideval, exec_1_portn_peripherals, peripherals_1_read, ramasync_1_q, registerfile_1_da,
       registerfile_1_db;
  wire [19:0] Instruction_Memory_d;

  not not_1 (not_1_out, peripherals_1_interrupt);
  ROM #(.AddrBits(8), .isProgramMemory("true"), .Bits(20)) Instruction_Memory (
    .A(out_2), .sel(1'b1), .D(Instruction_Memory_d));
  decoder decoder_1 (
    .Inst(Instruction_Memory_d), .Opcode(decoder_1_opcode), .Reg_1(Reg_1), .Reg_2(Reg_2), .Val_IMMPTR(out_3),
    .Mode(decoder_1_mode));
  and and_1 (and_1_out, HLT_Flag, not_1_out);
  D_FF d_ff_1 (.D(Clk_t), .C(Clk_t), .Q(d_ff_1_q));  // open: nQ
  CounterPreset #(.Bits(8), .isProgramCounter("true")) counterpreset_1 (
    .en(1'b1), .C(Clk_2), .dir(1'b0), .in(exec_1_pc_overrideval), .ld(exec_1_pc_override), .clr(1'b0),
    .out(out_2), .ovf(Overflow));
  or or_1 (Clk_t, clk, and_1_out);
  and and_2 (Clk_2, not_2_out, d_ff_1_q);
  not not_2 (not_2_out, Clk_t);
  RegisterFile #(.AddrBits(3), .Bits(8)) registerfile_1 (
    .Din(exec_1_din_rf), .we(exec_1_we_rf), .Rw(exec_1_rw_rf), .C(Clk_t), .Ra(exec_1_ra_rf),
    .Rb(exec_1_rb_rf), .Da(registerfile_1_da), .Db(registerfile_1_db));
  RAMAsync #(.AddrBits(8), .Bits(8)) ramasync_1 (.A(exec_1_a_ram), .D(exec_1_d_ram), .we(and_3_out), .Q(ramasync_1_q));
  exec exec_1 (
    .Opcode(decoder_1_opcode), .Da_RF(registerfile_1_da), .Db_RF(registerfile_1_db), .Reg_1(Reg_1),
    .Reg_2(Reg_2), .Val_IMMPTR(out_3), .Q_RAM(ramasync_1_q), .O_ALU(out_4), .Mode(decoder_1_mode),
    .Read_Peripherals(peripherals_1_read), .A_ALU(exec_1_a_alu), .Din_RF(exec_1_din_rf),
    .RW_RF(exec_1_rw_rf), .WE_RF(exec_1_we_rf), .A_RAM(exec_1_a_ram), .D_RAM(exec_1_d_ram),
    .WE_RAM(exec_1_we_ram), .PC_Override(exec_1_pc_override), .PC_OverrideVal(exec_1_pc_overrideval),
    .HLT_Flag(HLT_Flag), .Ra_RF(exec_1_ra_rf), .Rb_RF(exec_1_rb_rf), .B_ALU(exec_1_b_alu),
    .PortN_Peripherals(exec_1_portn_peripherals), .Data_Peripherals(exec_1_data_peripherals),
    .Write_Peripherals(exec_1_write_peripherals), .ReadSig_Peripherals(exec_1_readsig_peripherals));
  and and_3 (and_3_out, exec_1_we_ram, Clk_t);
  alu alu_1 (.A(exec_1_a_alu), .B(exec_1_b_alu), .Opcode(decoder_1_opcode), .O(out_4));
  peripherals peripherals_1 (
    .PortN(exec_1_portn_peripherals), .Data(exec_1_data_peripherals), .Clk(Clk_2),
    .Write(exec_1_write_peripherals), .WClk(Clk_t), .ReadSig(exec_1_readsig_peripherals),
    .Read(peripherals_1_read), .Interrupt(peripherals_1_interrupt));

  // Other names for the same wires on the sheet: PC[7:0] = out_2

  // Notes on the sheet:
  //   clk: Hz: 50
  //   contents of Instruction_Memory (hex, n*v repeats v):
  //   e1fe,c002,2e800,de000,c004,2e800,de000,c006,2e800,de000,d6000
  //   ,13c01,d6000,12c01,d6000,11c01
endmodule
