// Digital circuit peripherals.dig as structural Verilog
module peripherals (
  input  [7:0] PortN,
  input  [7:0] Data,
  input  Clk,
  input  Write,
  input  WClk,
  input  ReadSig,
  output [7:0] Read,
  output Interrupt
);

  wire [7:0] keyboard_1_d;
  wire [15:8] keyboard_1_d_2;

  Terminal terminal_1 (.D(Data), .C(WClk), .en(Write));
  Keyboard keyboard_1 (.C(Clk), .en(ReadSig), .D({keyboard_1_d_2, keyboard_1_d}), .av(Interrupt));
  Multiplexer #(.Bits(8)) multiplexer_1 (.sel(PortN[0]), .in_0({8{1'b0}}), .in_1(keyboard_1_d), .out(Read));
endmodule
